# Fritzing sketch Joystick02 (saved by Fritzing 0.9.9b)

parts:
  U1 = LuaNode32 / ESP32 [part_number=ESP32S-PIN30]  # not connected
  Part4 = Arduino Joystick Shield
  A1 = DORHEA ESP32 GPIO breakout board 30pin
  Raspberry_Pi_1 = Raspberry Pi 4 [part_number=RPI-4-b]

nets:
  N1: Part4.3.3V, A1.Pin_14, A1.Pin_114
  N2: Part4.VERTICAL, A1.Pin_10
  N3: Part4.A2, A1.Pin_9
  N4: Part4.SEL, A1.Pin_8
  N5: Part4.D3, A1.Pin_7
  N6: Part4.D4, A1.Pin_6
  N7: Part4.D5, A1.Pin_5
  N8: Part4.D6, A1.Pin_4
  N9: Part4.D7, A1.Pin_3
  N10: Part4.D8, A1.Pin_1, A1.Pin_2
  N11: A1.Pin_27, A1.Pin_28, A1.Pin_85, Raspberry_Pi_1.GND
  N12: A1.Pin_61, A1.Pin_62, Raspberry_Pi_1.3v3
  N13: A1.Pin_116, Raspberry_Pi_1.GPIO23
  N14: A1.Pin_117, Raspberry_Pi_1.GPIO24

custom parts:
  LuaNode32 / ESP32: New Image for LuaNode32 DOIT ESP32 DEVKIT V1. Base parts from LuaNode32 / ESP32 ESP32 based LuaNode32 by G.Noorlander DOIT Esp32 DevKit v1 (30 pins long, 11 pins width) by Werner Rothschopf (modified by vanepp Dec 2018)
  DORHEA ESP32 GPIO breakout board 30pin: ESP32 shield 30P expansion board, supports two power supply : DC 6.5-16v and USB 5.V
  Raspberry Pi 4: The RPi4, a faster version of the awesome Raspberry Pi 2 B ARM Board with 40 pin gpio. Ready for special Raspberry Pi B+ and RPi2 Hat (Hardware attached (on) top)
