# Fritzing sketch JoystickDevTitans (saved by Fritzing 0.9.9b)
breadboards: 1

parts:
  Raspberry_Pi_1 = raspberry_pi_4 [part_number=RPI-4-b]
  S1 = Momentary Switch [package=ksa_sealed_tac_switch]
  S2 = Momentary Switch [package=ksa_sealed_tac_switch]
  S3 = Momentary Switch [package=ksa_sealed_tac_switch]
  S4 = Momentary Switch [package=ksa_sealed_tac_switch]
  R1 = Resistor [tolerance=±5% power=0.25W resistance=220 package=THT]
  R2 = Resistor [tolerance=±5% power=0.25W resistance=220 package=THT]
  R3 = Resistor [tolerance=±5% power=0.25W resistance=220 package=THT]
  R4 = Resistor [tolerance=±5% power=0.25W resistance=220 package=THT]
  U2 = JOYSTICK-PSP1000 [package=joystick-psp1000]
  Raspberry_Pi_2 = raspberry_pi_4 [part_number=RPI-4-b]
  Componente1 = Arduino Joystick Shield
  U3 = LuaNode32_ESP32_r1 [part_number=ESP32S-PIN30]
  U4 = LuaNode32_ESP32_r1 [part_number=ESP32S-PIN30]

nets:
  N1: Raspberry_Pi_1.connector0, S1.4, S2.4, S3.4, S4.4, U2.VCC, U4.connector15
  N2: Raspberry_Pi_1.connector37, R1.Pin_1, R2.Pin_1, R3.Pin_1, R4.Pin_1, U2.GND, U4.connector16
  N3: S1.2, R2.Pin_0
  N4: S2.2, R3.Pin_0
  N5: S3.2, R4.Pin_0
  N6: S4.2, R1.Pin_0
  N7: U2.X, U4.connector19
  N8: U2.Y, U4.connector18
  N9: Raspberry_Pi_2.connector35, U3.connector3
  N10: Raspberry_Pi_2.connector36, U3.connector4
  N11: Raspberry_Pi_2.connector37, U3.connector13
  N12: Raspberry_Pi_2.connector38, U3.connector14
  N13: Componente1.3.3V, U3.connector15
  N14: Componente1.VERTICAL, U3.connector19
  N15: Componente1.HORIZONTAL, U3.connector18
  N16: Componente1.D3, U3.connector10
  N17: Componente1.D4, U3.connector9
  N18: Componente1.D5, U3.connector6
  N19: Componente1.D6, U3.connector5
  N20: Componente1.D7, U3.connector2
  N21: Componente1.D8, U3.connector1
